// Logisim project 8bit-cpu.circ as structural Verilog: 6 circuits, main circuit main
module main (
);

  Registers_Module registers_module_1 ();  // open: readSelect, dataIn, clk, clear, writeSelect, writeEnable, dataOut
  ALU alu_1 ();  // open: ALUOP2, ALUOP1, ALUOP0, Wreg, Rn, Result, carryF, zeroF
  ROM_module rom_module_1 ();  // open: addr, enable, data
  RAM_module ram_module_1 ();  // open: addr, dataIn, readEnable, writeEnable, clk, dataOut
endmodule

module ALU (
  input  ALUOP2,
  input  ALUOP1,
  input  ALUOP0,
  input  [7:0] Wreg,
  input  [7:0] Rn,
  output [7:0] Result,
  output carryF,
  output zeroF
);

  wire and_2_out, and_3_out, and_4_out, not_3_out, not_4_out, xor_2_out;
  wire [7:0] adder_1_out, adder_2_out, and_1_out, multiplexer_1_out, multiplexer_2_out, multiplexer_3_out,
       multiplexer_4_out, not_1_out, not_2_out, or_1_out, xor_1_out;

  assign not_1_out = ~Wreg;  // NOT_Gate not_1, 8 bits wide
  Adder adder_1 (.a(8'h1), .b(not_2_out), .out(adder_1_out));  // open: cin, cout
  assign not_2_out = ~Rn;  // NOT_Gate not_2, 8 bits wide
  assign and_1_out = Wreg & Rn;  // AND_Gate and_1, 8 bits wide
  assign or_1_out = Wreg | Rn;  // OR_Gate or_1, 8 bits wide
  assign xor_1_out = Wreg ^ Rn;  // XOR_Gate xor_1, 8 bits wide
  and and_2 (and_2_out, ALUOP1, ALUOP2);
  Multiplexer #(.width(8)) multiplexer_1 (.in0(Rn), .in1(adder_1_out), .out(multiplexer_1_out), .sel(ALUOP0));
  Multiplexer #(.width(8)) multiplexer_2 (.in0(8'h1), .in1({8{1'b1}}), .out(multiplexer_2_out), .sel(ALUOP0));
  Multiplexer #(.width(8)) multiplexer_3 (
    .in0(multiplexer_1_out), .in1(multiplexer_2_out), .out(multiplexer_3_out), .sel(and_2_out));
  not not_3 (not_3_out, ALUOP1);
  not not_4 (not_4_out, ALUOP2);
  Adder adder_2 (.a(Wreg), .b(multiplexer_3_out), .out(adder_2_out), .cout(carryF));  // open: cin
  and and_3 (and_3_out, not_3_out, ALUOP2);
  and and_4 (and_4_out, ALUOP1, not_4_out);
  xor xor_2 (xor_2_out, and_3_out, and_4_out);
  Multiplexer #(.select(3), .width(8)) multiplexer_4 (
    .in2(and_1_out), .in3(or_1_out), .in4(xor_1_out), .in5(not_1_out), .out(multiplexer_4_out),
    .sel({ALUOP2, ALUOP1, ALUOP0}));  // open: in0, in1, in6, in7
  Multiplexer #(.width(8)) multiplexer_5 (.in0(adder_2_out), .in1(multiplexer_4_out), .out(Result), .sel(xor_2_out));
  Comparator comparator_1 (.a({8{1'b0}}), .b(adder_2_out), .eq(zeroF));  // open: gt, lt
endmodule

module ROM_module (
  input  [7:0] addr,
  input  enable,
  output [7:0] data
);

  wire [7:0] rom_1_data;

  ROM rom_1 (.addr(addr), .data(rom_1_data));
  assign data = enable ? rom_1_data : 8'bz;  // Controlled_Buffer controlled_buffer_1

  // Notes on the sheet:
  //   contents of rom_1 (hex, n*v repeats v):
  //   11
endmodule

module RAM_module (
  input  [7:0] addr,
  input  [7:0] dataIn,
  input  readEnable,
  input  writeEnable,
  input  clk,
  output [7:0] dataOut
);

  wire [7:0] ram_1_dout;

  RAM ram_1 (.addr(addr), .we(writeEnable), .oe(readEnable), .clk(clk), .din(dataIn), .dout(ram_1_dout));
  assign dataOut = readEnable ? ram_1_dout : 8'bz;  // Controlled_Buffer controlled_buffer_1
endmodule

module Registers_Module (
  input  [2:0] readSelect,
  input  [7:0] dataIn,
  input  clk,
  input  clear,
  input  [2:0] writeSelect,
  input  writeEnable,
  output [7:0] dataOut
);

  wire decoder_1_out0, decoder_1_out1, decoder_1_out2, decoder_1_out3, decoder_1_out4, decoder_1_out5,
       decoder_1_out6, decoder_1_out7;
  wire [7:0] MA_q, MD_q, R0_q, R1_q, R2_q, R3_q, SP_q, Wreg_q;

  Decoder #(.select(3)) decoder_1 (
    .out0(decoder_1_out0), .out1(decoder_1_out1), .out2(decoder_1_out2), .out3(decoder_1_out3),
    .out4(decoder_1_out4), .out5(decoder_1_out5), .out6(decoder_1_out6), .out7(decoder_1_out7),
    .sel(writeSelect), .en(writeEnable));
  Register Wreg (.D(dataIn), .en(decoder_1_out0), .clk(clk), .Q(Wreg_q), .clr(clear));
  Register R0 (.D(dataIn), .en(decoder_1_out1), .clk(clk), .Q(R0_q), .clr(clear));
  Register R1 (.D(dataIn), .en(decoder_1_out2), .clk(clk), .Q(R1_q), .clr(clear));
  Register R2 (.D(dataIn), .en(decoder_1_out3), .clk(clk), .Q(R2_q), .clr(clear));
  Register R3 (.D(dataIn), .en(decoder_1_out4), .clk(clk), .Q(R3_q), .clr(clear));
  Register SP (.D(dataIn), .en(decoder_1_out5), .clk(clk), .Q(SP_q), .clr(clear));
  Register MD (.D(dataIn), .en(decoder_1_out6), .clk(clk), .Q(MD_q), .clr(clear));
  Register MA (.D(dataIn), .en(decoder_1_out7), .clk(clk), .Q(MA_q), .clr(clear));
  Multiplexer #(.select(3), .width(8)) multiplexer_1 (
    .in0(Wreg_q), .in1(R0_q), .in2(R1_q), .in3(R2_q), .in4(R3_q), .in5(SP_q), .in6(MD_q), .in7(MA_q),
    .out(dataOut), .sel(readSelect));
endmodule

module ControlUnit_module (
  input  [4:0] opcode,
  input  clk,
  input  zeroF,
  input  carryF,
  output Wreg_WE,
  output REG_WE,
  output [2:0] REG_SEL,
  output RAM_RE,
  output RAM_WE,
  output RAM_ADDR_EN,
  output [2:0] ALU_OP,
  output ALU_EN,
  output PC_LOAD,
  output PC_EN,
  output SP_INC,
  output SP_DEC,
  output STACK_WE,
  output STACK_RE,
  output HALT
);

  wire decoder_1_out0, decoder_1_out1, decoder_1_out2, decoder_1_out3, decoder_1_out4, decoder_1_out5,
       decoder_1_out6, decoder_1_out7, decoder_1_out8, decoder_1_out9, decoder_1_out10, decoder_1_out11,
       decoder_1_out12, decoder_1_out13, decoder_1_out14, decoder_1_out15, decoder_1_out16, decoder_1_out17,
       decoder_1_out18, decoder_1_out19;

  Decoder #(.select(5)) decoder_1 (
    .out0(decoder_1_out0), .out1(decoder_1_out1), .out2(decoder_1_out2), .out3(decoder_1_out3),
    .out4(decoder_1_out4), .out5(decoder_1_out5), .out6(decoder_1_out6), .out7(decoder_1_out7),
    .out8(decoder_1_out8), .out9(decoder_1_out9), .out10(decoder_1_out10), .out11(decoder_1_out11),
    .out12(decoder_1_out12), .out13(decoder_1_out13), .out14(decoder_1_out14), .out15(decoder_1_out15),
    .out16(decoder_1_out16), .out17(decoder_1_out17), .out18(decoder_1_out18), .out19(decoder_1_out19),
    .sel(opcode));  // open: out20, out21, out22, out23, out24, out25, out26, out27, out28, out29, out30, out31, en
  not not_1 (ALU_EN, decoder_1_out0);
  not not_2 (PC_EN, ALU_EN);

  assign HALT = ALU_EN;
  assign PC_LOAD = ALU_EN;
  assign RAM_ADDR_EN = ALU_EN;
  assign RAM_RE = ALU_EN;
  assign RAM_WE = ALU_EN;
  assign REG_WE = ALU_EN;
  assign SP_DEC = ALU_EN;
  assign SP_INC = ALU_EN;
  assign STACK_RE = ALU_EN;
  assign STACK_WE = ALU_EN;
  assign Wreg_WE = ALU_EN;

  // Notes on the sheet:
  //   NOP
endmodule
